// Logisim project lab3.circ as structural Verilog
module one_bit_adder (
  input  A,
  input  B,
  input  C_In,
  output Sum,
  output C_Out
);

  wire and_1_out, and_2_out, xor_1_out;

  xor xor_1 (xor_1_out, A, B);
  and and_1 (and_1_out, xor_1_out, C_In);
  and and_2 (and_2_out, A, B);
  xor xor_2 (Sum, xor_1_out, C_In);
  or or_1 (C_Out, and_1_out, and_2_out);
endmodule

module one_bit_ALU (
  input  [3:0] ALU_Ctrl,
  input  A,
  input  B,
  input  C_In,
  output R,
  output C_Out
);

  wire and_1_out, multiplexer_1_out, not_1_out, one_bit_adder_1_sum, or_1_out, xor_1_out;

  not not_1 (not_1_out, B);
  Multiplexer #(.enable("false")) multiplexer_1 (.in0(B), .in1(not_1_out), .out(multiplexer_1_out), .sel(ALU_Ctrl[2]));
  and and_1 (and_1_out, A, multiplexer_1_out);
  or or_1 (or_1_out, A, multiplexer_1_out);
  xor xor_1 (xor_1_out, A, multiplexer_1_out);
  one_bit_adder one_bit_adder_1 (.A(A), .B(multiplexer_1_out), .C_In(C_In), .Sum(one_bit_adder_1_sum), .C_Out(C_Out));
  Multiplexer #(.enable("false"), .select(2)) multiplexer_2 (
    .in0(and_1_out), .in1(or_1_out), .in2(xor_1_out), .in3(one_bit_adder_1_sum), .out(R), .sel(ALU_Ctrl[1:0]));
endmodule

module ALU4 (
  input  [3:0] ALU_Ctrl,
  input  C_In,
  input  [3:0] A,
  input  [3:0] B,
  output [3:0] R,
  output C_Out
);

  wire one_bit_alu_1_c_out, one_bit_alu_2_c_out, one_bit_alu_3_c_out;

  one_bit_ALU one_bit_alu_1 (
    .ALU_Ctrl(ALU_Ctrl), .A(A[0]), .B(B[0]), .C_In(C_In), .R(R[0]), .C_Out(one_bit_alu_1_c_out));
  one_bit_ALU one_bit_alu_2 (
    .ALU_Ctrl(ALU_Ctrl), .A(A[1]), .B(B[1]), .C_In(one_bit_alu_1_c_out), .R(R[1]), .C_Out(one_bit_alu_2_c_out));
  one_bit_ALU one_bit_alu_3 (
    .ALU_Ctrl(ALU_Ctrl), .A(A[2]), .B(B[2]), .C_In(one_bit_alu_2_c_out), .R(R[2]), .C_Out(one_bit_alu_3_c_out));
  one_bit_ALU one_bit_alu_4 (
    .ALU_Ctrl(ALU_Ctrl), .A(A[3]), .B(B[3]), .C_In(one_bit_alu_3_c_out), .R(R[3]), .C_Out(C_Out));
endmodule

module ALU16 (
  input  [3:0] ALU_Ctrl,
  input  C_In,
  input  [15:0] A,
  input  [15:0] B,
  output [15:0] R,
  output C_Out
);

  wire alu4_1_c_out, alu4_2_c_out, alu4_3_c_out;

  ALU4 alu4_1 (.ALU_Ctrl(ALU_Ctrl), .C_In(C_In), .A(A[3:0]), .B(B[3:0]), .R(R[3:0]), .C_Out(alu4_1_c_out));
  ALU4 alu4_2 (.ALU_Ctrl(ALU_Ctrl), .C_In(alu4_1_c_out), .A(A[7:4]), .B(B[7:4]), .R(R[7:4]), .C_Out(alu4_2_c_out));
  ALU4 alu4_3 (.ALU_Ctrl(ALU_Ctrl), .C_In(alu4_2_c_out), .A(A[11:8]), .B(B[11:8]), .R(R[11:8]), .C_Out(alu4_3_c_out));
  ALU4 alu4_4 (.ALU_Ctrl(ALU_Ctrl), .C_In(alu4_3_c_out), .A(A[15:12]), .B(B[15:12]), .R(R[15:12]), .C_Out(C_Out));
endmodule

module ALU32 (
  input  [3:0] ALU_Ctrl,
  input  C_In,
  input  [31:0] A,
  input  [31:0] B,
  output [31:0] R,
  output C_Out
);

  wire alu16_1_c_out;

  ALU16 alu16_1 (.ALU_Ctrl(ALU_Ctrl), .C_In(C_In), .A(A[15:0]), .B(B[15:0]), .R(R[15:0]), .C_Out(alu16_1_c_out));
  ALU16 alu16_2 (.ALU_Ctrl(ALU_Ctrl), .C_In(alu16_1_c_out), .A(A[31:16]), .B(B[31:16]), .R(R[31:16]), .C_Out(C_Out));
endmodule

module ALU_Control (
  input  I30,
  input  I14,
  input  I13,
  input  I12,
  input  I6,
  input  I5,
  input  I4,
  output ALU_Ctrl3,
  output ALU_Ctrl2,
  output ALU_Ctrl1,
  output ALU_Ctrl0,
  output ALU_Src
);

  wire and_2_out, not_1_out, not_2_out, not_3_out, not_4_out, not_5_out;

  not not_1 (not_1_out, I14);
  not not_2 (not_2_out, I13);
  not not_3 (not_3_out, I12);
  not not_4 (not_4_out, I5);
  not not_5 (not_5_out, I4);
  and and_1 (ALU_Ctrl2, I30, not_2_out, I5);
  or or_1 (ALU_Ctrl1, not_2_out, not_5_out);
  and and_2 (and_2_out, I13, not_3_out);
  or or_2 (ALU_Src, not_4_out, not_5_out);
  or or_3 (ALU_Ctrl0, not_1_out, and_2_out);

  assign ALU_Ctrl3 = 1'b0;
endmodule
